# Fritzing sketch Circuit_03_Alteration_1 (saved by Fritzing 0.9.2b)
breadboards: 1

parts:
  Part2 = Arduino Uno (Rev3)
  R1 = Resistor [tolerance=±5% resistance=330 package="0402 [SMD]"]
  R2 = Resistor [tolerance=±5% resistance=330 package="0402 [SMD]"]
  R3 = Resistor [tolerance=±5% resistance=330 package="0402 [SMD]"]
  LED1 = RGB LED - (4 legs) [package="5 mm [THT]"]
  R4 = TRIMPOT [package=3386u]

nets:
  N1: Part2.A0, R4.WIPER
  N2: Part2.D11_PWM/MOSI, R1.Pin_1
  N3: Part2.D12/MISO, R2.Pin_1
  N4: Part2.D13/SCK, R3.Pin_1
  N5: Part2.5V, R4.CW
  N6: Part2.GND, LED1.green_cathode, R4.CCW
  N7: R1.Pin_0, LED1.red_cathode
  N8: R2.Pin_0, LED1.common_anode
  N9: R3.Pin_0, LED1.blue_cathode
