# Fritzing sketch Circuit_09_Alteration_2 (saved by Fritzing 0.9.2b)
breadboards: 1

parts:
  Part2 = Arduino Uno (Rev3)
  R4 = TRIMPOT [package=3386u]
  J1 = Piezo Speaker

nets:
  N1: Part2.A0, R4.WIPER
  N2: Part2.D9_PWM, J1.pin2
  N3: Part2.5V, R4.CW
  N4: Part2.GND, R4.CCW, J1.pin1
