# Fritzing sketch Circuit_10_Alteration_1 (saved by Fritzing 0.9.2b)
breadboards: 1

parts:
  Part2 = Arduino Uno (Rev3)
  R4 = TRIMPOT [package=3386u]
  M1 = DC Motor
  Q1 = TRANSISTOR_PNP [package=to-92]
  R5 = Resistor [tolerance=±5% resistance=220 package="0402 [SMD]"]
  D1 = Rectifier Diode [part_number=1N4001 package="Melf DO-213 AB [SMD]"]

nets:
  N1: Part2.A0, R4.WIPER
  N2: Part2.D9_PWM, R5.Pin_1
  N3: Part2.5V, R4.CW
  N4: Part2.GND, R4.CCW
  N5: M1.pin_1, D1.cathode
  N6: M1.pin_2, Q1.E, D1.anode
  N7: Q1.B, R5.Pin_0
