# Fritzing sketch simon (saved by Fritzing 0.9.2b)
breadboards: 1

parts:
  Part2 = Arduino Uno (Rev3)
  J1 = Piezo Speaker
  S3 = Pushbutton [package="[SMD]"]
  S2 = Pushbutton [package="[SMD]"]
  S1 = Pushbutton [package="[SMD]"]
  S4 = Pushbutton [package="[SMD]"]
  NEOPIXEL2 = Neopixel Strip -- Black (30/m)
  R3 = Resistor [tolerance=±5% resistance=330 package=THT]
  C2 = Electrolytic Capacitor [capacitance=100n package="100 mil [THT, electrolytic]"]

nets:
  N1: Part2.D8, S2.Pin_1, S2.Pin_2
  N2: Part2.D10_PWM/SS, S3.Pin_1, S3.Pin_2
  N3: Part2.D12/MISO, S4.Pin_1, S4.Pin_2
  N4: Part2.D13/SCK, J1.pin2
  GND: Part2.GND, J1.pin1, S3.Pin_3, S3.Pin_4, S2.Pin_3, S2.Pin_4, S1.Pin_3, S1.Pin_4, S4.Pin_3, S4.Pin_4, NEOPIXEL2.GND, C2.-
  N5: Part2.D2, R3.Pin_1
  N6: Part2.D6_PWM, S1.Pin_1, S1.Pin_2
  5V: Part2.5V, NEOPIXEL2.+5V
  N7: NEOPIXEL2.Din, R3.Pin_0

custom parts:
  Neopixel Strip -- Black (30/m): These NeoPixel strips have 30 digitally-addressable pixel LEDs per meter and are very affordable and are only 12.5 mm wide, 10 mm if you remove the strip from the casing.
