# Fritzing sketch button_led_wiring_diagram (saved by Fritzing 0.9.2b)
breadboards: 1

parts:
  Part1 = Arduino Uno (Rev3)
  R1 = Resistor [tolerance=±5% resistance=220 package=THT]
  LED1 = LED - 5mm [color="Red (633nm)" package="5 mm [THT]"]
  S1 = Pushbutton [package="[THT]"]

nets:
  N1: Part1.GND, R1.Pin_1
  N2: Part1.5V, S1.Pin_3, S1.Pin_4
  N3: R1.Pin_0, LED1.cathode
  N4: LED1.anode, S1.Pin_1, S1.Pin_2
