# Fritzing sketch button_ws2811_wiring_diagram (saved by Fritzing 0.9.2b)
breadboards: 1

parts:
  Part1 = Arduino Ethernet Shield (Rev3)
  NEOPIXEL1 = Neopixel Strip -- Black (30/m)
  S3 = Pushbutton [package="[THT]"]
  S2 = Pushbutton [package="[THT]"]
  S1 = Pushbutton [package="[THT]"]
  R2 = Resistor [tolerance=±5% resistance=330 package=THT]
  C1 = Electrolytic Capacitor [capacitance=100n package="100 mil [THT, electrolytic]"]

nets:
  N1: Part1.ETH_CS, S2.Pin_3, S2.Pin_4
  N2: Part1.SPI/D12, S1.Pin_3, S1.Pin_4
  GND: Part1.GND, NEOPIXEL1.GND, S3.Pin_3, S3.Pin_4, S2.Pin_1, S2.Pin_2, S1.Pin_1, S1.Pin_2, C1.-
  N3: Part1.D2, R2.Pin_1
  N4: Part1.D7, S3.Pin_1, S3.Pin_2
  5V: Part1.5V, NEOPIXEL1.+5V, C1.+
  N5: NEOPIXEL1.Din, R2.Pin_0

custom parts:
  Neopixel Strip -- Black (30/m): These NeoPixel strips have 30 digitally-addressable pixel LEDs per meter and are very affordable and are only 12.5 mm wide, 10 mm if you remove the strip from the casing.
