# Fritzing sketch ethernet_dht11 (saved by Fritzing 0.9.2b)
breadboards: 1

parts:
  DHT1 = DHT11 Humitidy and Temperature Sensor
  Part1 = Arduino Ethernet Shield (Rev3)

nets:
  VDD: DHT1.VDD, Part1.5V
  N1: DHT1.DATA, Part1.PWM_D3
  GND: DHT1.GND, Part1.GND

custom parts:
  DHT11 Humitidy and Temperature Sensor: DHT11 Humidity and Temperature Sensor
