# Fritzing sketch photoresistor_nopcb_ethernet (saved by Fritzing 0.9.2b)
breadboards: 1

parts:
  R2 = Resistor [tolerance=±5% resistance=220 package=THT]
  R1 = PHOTOCELL [package=photocell-kit]
  R3 = Resistor [tolerance=±5% resistance=220 package=THT]
  LED1 = LED - 5mm [color="Red (633nm)" package="5 mm [THT]"]
  Part1 = Arduino Ethernet Shield (Rev3)

nets:
  N1: R2.Pin_0, R1.P$1, Part1.A0
  N2: R2.Pin_1, Part1.5V
  N3: R1.P$2, R3.Pin_0, Part1.GND
  N4: R3.Pin_1, LED1.cathode
  N5: LED1.anode, Part1.PWM_D9
