# Fritzing sketch ws2811_neo_pixel_strip_external_power (saved by Fritzing 0.9.2b)
breadboards: 1

parts:
  R2 = Resistor [tolerance=±5% resistance=330 package=THT]
  Part1 = Arduino Ethernet Shield (Rev3)
  C1 = Electrolytic Capacitor [capacitance=100nF package="100 mil [THT, electrolytic]"]
  NEOPIXEL1 = Neopixel Strip -- Black (30/m)
  VCC1 = 4 x AAA Battery Mount

nets:
  N1: R2.Pin_0, NEOPIXEL1.Din
  N2: R2.Pin_1, Part1.PWM_D5
  GND: Part1.GND, C1.-, NEOPIXEL1.GND, VCC1.-
  N3: C1.+, VCC1.+

custom parts:
  Neopixel Strip -- Black (30/m): These NeoPixel strips have 30 digitally-addressable pixel LEDs per meter and are very affordable and are only 12.5 mm wide, 10 mm if you remove the strip from the casing.
